# Fritzing sketch schematic (saved by Fritzing 1.0.1rc)
breadboards: 1

parts:
  Mod1 = Raspberry Pi 4B
  R1 = Resistor [tolerance=±5% power=0.25W resistance=220 package=THT]
  LED1 = LED - 5mm [color="Red (633nm)" current=0.030A package="5 mm [THT]"]
  S1 = Pushbutton [package="[THT]"]
  S2 = Pushbutton [package="[THT]"]

nets:
  N1: Mod1.3V3, S1.Pin_3, S1.Pin_4, S2.Pin_3, S2.Pin_4
  N2: Mod1.GND, LED1.cathode
  N3: Mod1.GPIO16, R1.Pin_0
  N4: Mod1.GPIO20, S2.Pin_1, S2.Pin_2
  N5: Mod1.GPIO21, S1.Pin_1, S1.Pin_2
  N6: R1.Pin_1, LED1.anode
