# Fritzing sketch schematic (saved by Fritzing 1.0.1rc)
breadboards: 1

parts:
  Mod1 = Raspberry Pi 4B
  S1 = Pushbutton [package="[THT]"]
  S2 = Pushbutton [package="[THT]"]
  LED1 = RGB LED (com. cathode, rgb) [color="Red (633nm)" current=0.030A package="5 mm [THT]"]
  R1 = Resistor [tolerance=±5% power=0.25W resistance=220 package=THT]
  R2 = Resistor [tolerance=±5% power=0.25W resistance=220 package=THT]
  R3 = Resistor [tolerance=±5% power=0.25W resistance=220 package=THT]
  S3 = Pushbutton [package="[THT]"]

nets:
  N1: Mod1.3V3, S1.Pin_3, S1.Pin_4, S2.Pin_3, S2.Pin_4, S3.Pin_3, S3.Pin_4
  N2: Mod1.GND, LED1.common_cathode
  N3: Mod1.GPIO13, R3.Pin_0
  N4: Mod1.GPIO19, R2.Pin_0
  N5: Mod1.GPIO16, S3.Pin_1, S3.Pin_2
  N6: Mod1.GPIO26, R1.Pin_0
  N7: Mod1.GPIO20, S2.Pin_1, S2.Pin_2
  N8: Mod1.GPIO21, S1.Pin_1, S1.Pin_2
  N9: LED1.red_anode, R1.Pin_1
  N10: LED1.green_anode, R2.Pin_1
  N11: LED1.blue_anode, R3.Pin_1
